# Fritzing sketch base_circuit01 (saved by Fritzing 0.8.5b)
breadboards: 1

parts:
  U1 = atmega328 [package=dip]
  R1 = Resistor [tolerance=±5% resistance=10k package=THT]
  C1 = Ceramic Capacitor [capacitance=100nF voltage=16V package="100 mil [THT, multilayer]"]
  C2 = Ceramic Capacitor [capacitance=100nF voltage=16V package="100 mil [THT, multilayer]"]
  C3 = Ceramic Capacitor [capacitance=100nF voltage=16V package="100 mil [THT, multilayer]"]
  Composants1 = FTDI Basic Programmer
  U2 = G3VM-61E1 [package=g3vm-61e1]
  J1 = Screw terminal - 2 pins [package=THT]
  LED1 = LED - 5mm [color="Red (633nm)" package="5 mm [THT]"]
  U3 = G3VM-61E1 [package=g3vm-61e1]
  J2 = Screw terminal - 2 pins [package=THT]
  LED2 = LED - 5mm [color="Orange (612nm)" package="5 mm [THT]"]
  U4 = TEMPERATURE-SENSOR [package=to-92]
  R2 = Resistor [tolerance=±5% resistance=4.7k package=THT]
  R3 = Resistor [tolerance=±5% resistance=10k package=THT]
  R4 = Resistor [tolerance=±5% resistance=4.7k package=THT]
  Raspberry_Pi_B_rev1 = Raspberry Pi B rev2

nets:
  N1: U1.RESET, R1.Pin_0, C3.1
  N2: U1.D0_(RX), Composants1.TXO, Raspberry_Pi_B_rev1.GPIO_14
  N3: U1.D1_(TX), Composants1.RXI, R4.Pin_1
  VCC: U1.VCC, U1.AVCC, R1.Pin_1, C1.1, C2.1, Composants1.POWER, U2.P$1, U3.P$1, U4.VCC, R2.Pin_0
  GND: U1.GND, C1.0, C2.0, Composants1.GND, U2.P$2, U3.P$2, U4.GND, R3.Pin_0, Raspberry_Pi_B_rev1.GND
  N4: U1.D8, U4.ADJ, R2.Pin_1
  N5: U1.D9_(PWM), U2.P$3
  N6: U1.D10_(PWM), U3.P$3
  N7: C3.0, Composants1.DTR
  N8: J1.pin2, LED1.anode
  N9: U3.P$5, J2.pin2, LED2.anode
  N10: U3.P$6, J2.pin1
  N11: R3.Pin_1, R4.Pin_0, Raspberry_Pi_B_rev1.GPIO_15
