# Fritzing sketch base_circuit02 (saved by Fritzing 0.8.5b)
breadboards: 1

parts:
  U1 = atmega328 [package=dip]
  R1 = Resistor [tolerance=±5% resistance=10k package=THT]
  C1 = Ceramic Capacitor [capacitance=100nF voltage=16V package="100 mil [THT, multilayer]"]
  C2 = Ceramic Capacitor [capacitance=100nF voltage=16V package="100 mil [THT, multilayer]"]
  C3 = Ceramic Capacitor [capacitance=100nF voltage=16V package="100 mil [THT, multilayer]"]
  Composants1 = FTDI Basic Programmer
  U2 = G3VM-61E1 [package=g3vm-61e1]
  J1 = Screw terminal - 2 pins [package=THT]
  LED1 = LED - 5mm [color="Red (633nm)" package="5 mm [THT]"]
  U3 = G3VM-61E1 [package=g3vm-61e1]
  J2 = Screw terminal - 2 pins [package=THT]
  LED2 = LED - 5mm [color="Orange (612nm)" package="5 mm [THT]"]
  U4 = TEMPERATURE-SENSOR [package=to-92]
  R2 = Resistor [tolerance=±5% resistance=4.7k package=THT]
  R3 = Resistor [tolerance=±5% resistance=10k package=THT]  # not connected
  R4 = Resistor [tolerance=±5% resistance=4.7k package=THT]
  Raspberry_Pi_B_rev1 = Raspberry Pi B rev2
  U5 = TEMPERATURE-SENSOR [package=to-92]
  R5 = Resistor [tolerance=±5% resistance=4.7k package=THT]  # not connected
  U6 = TEMPERATURE-SENSOR [package=to-92]
  R6 = Resistor [tolerance=±5% resistance=4.7k package=THT]  # not connected
  Q1 = Basic FET P-Channel [part_number=TIP120 package="TO220 [THT]"]
  R7 = Resistor [tolerance=±5% resistance=2.2k package=THT]
  M1 = DC Motor
  D1 = Rectifier Diode [part_number=1N4001 package="300 mil [THT]"]
  Q2 = Basic FET P-Channel [part_number=TIP120 package="TO220 [THT]"]
  R8 = Resistor [tolerance=±5% resistance=2.2k package=THT]
  D2 = Rectifier Diode [part_number=1N4001 package="300 mil [THT]"]
  J3 = Peltier Element

nets:
  N1: U1.RESET, R1.Pin_0, C3.1
  N2: U1.D0_(RX), Composants1.TXO, Raspberry_Pi_B_rev1.GPIO_14
  N3: U1.D1_(TX), Composants1.RXI, R4.Pin_1
  VCC: U1.VCC, U1.AVCC, R1.Pin_1, C1.1, C2.1, Composants1.POWER, U2.P$1, U3.P$1, U4.VCC, R2.Pin_0, U5.VCC, U6.VCC
  GND: U1.GND, C1.0, C2.0, Composants1.GND, U2.P$2, U3.P$2, U4.GND, Raspberry_Pi_B_rev1.GND, U5.GND, U6.GND, Q1.source, Q2.source
  N4: U1.D6_(PWM), U6.ADJ
  N5: U1.D7, U5.ADJ
  N6: U1.D8, U4.ADJ, R2.Pin_1
  N7: U1.D9_(PWM), U2.P$3
  N8: U1.D10_(PWM), U3.P$3
  N9: U1.D11_(PWM), R7.Pin_1
  N10: U1.D12, R8.Pin_0
  N11: C3.0, Composants1.DTR
  N12: U2.P$5, J1.pin2, LED1.anode
  N13: U2.P$6, J1.pin1
  N14: U3.P$5, J2.pin2, LED2.anode
  N15: U3.P$6, J2.pin1
  N16: R4.Pin_0, Raspberry_Pi_B_rev1.GPIO_15
  N17: Q1.gate, R7.Pin_0
  N18: Q1.drain, M1.pin_2, D1.anode
  N19: M1.pin_1, D1.cathode
  N20: Q2.drain, D2.anode, J3.pin1
  N21: D2.cathode, J3.pin2
